// Logisim project var10.circ as structural Verilog: 1 circuit, main circuit main
module main (
  input  [3:0] \Вход ,
  input  [3:0] \Делитель ,
  output \Симметричность 
);

  wire xnor_1_out, xnor_2_out;
  wire [3:0] divider_1_out, divider_1_rem;

  xnor xnor_1 (xnor_1_out, \Вход [1], \Вход [2]);
  // Probe on \Вход 
  xnor xnor_2 (xnor_2_out, \Вход [0], \Вход [3]);
  and and_1 (\Симметричность , xnor_1_out, xnor_2_out);
  // Probe on \Делитель 
  // Probe on divider_1_out
  // Probe on divider_1_rem
  Divider #(.width(4)) divider_1 (.a(\Вход ), .b(\Делитель ), .out(divider_1_out), .rem(divider_1_rem));  // open: upper
  // Probe on divider_1_rem

  // Notes on the sheet:
  //   Вариант 10
  //   Выполнил Соколов Арсений
endmodule
