// Logisim project var8.circ as structural Verilog: 2 circuits, main circuit main
module main (
  input  [4:0] in_1,
  input  [4:0] in_2,
  output [4:0] out_3,
  output [4:0] out_4
);

  wire and_1_out, not_1_out, not_2_out, not_3_out, not_4_out, not_5_out, xor_1_out, xor_2_out, xor_3_out,
       xor_4_out;
  wire [1:0] adder_1_out, adder_2_out, bit_extender_1_out, bit_extender_2_out, bit_extender_3_out;

  // Probe on in_1
  not not_1 (not_1_out, in_1[4]);
  xor xor_1 (xor_1_out, not_1_out, not_2_out);
  xor xor_2 (xor_2_out, not_2_out, not_3_out);
  not not_2 (not_2_out, in_1[3]);
  not not_3 (not_3_out, in_1[2]);
  not not_4 (not_4_out, in_1[1]);
  not not_5 (not_5_out, in_1[0]);
  xor xor_3 (xor_3_out, not_3_out, not_4_out);
  and and_1 (and_1_out, xor_2_out, xor_3_out);
  assign bit_extender_1_out = {{1{1'b0}}, xor_1_out};  // Bit_Extender bit_extender_1
  xor xor_4 (xor_4_out, not_4_out, not_5_out);
  assign bit_extender_2_out = {{1{1'b0}}, and_1_out};  // Bit_Extender bit_extender_2
  Adder #(.width(2)) adder_1 (.a(bit_extender_2_out), .b(bit_extender_1_out), .out(adder_1_out));  // open: cin, cout
  assign bit_extender_3_out = {{1{1'b0}}, xor_4_out};  // Bit_Extender bit_extender_3
  // Probe on in_2
  // Probe on adder_2_out
  Adder #(.width(2)) adder_2 (.a(bit_extender_3_out), .b(adder_1_out), .out(adder_2_out));  // open: cin, cout
  // Probe on out_3
  Divider #(.width(5)) divider_1 (.a(in_1), .b(in_2), .out(out_3), .rem(out_4));  // open: upper
  // Probe on out_4

  // Notes on the sheet:
  //   Вариант 8
  //   Выполнил Соколов Арсений
endmodule

module \олег  (
  input  a,
  input  b,
  input  c,
  input  d,
  input  e,
  output a_2,
  output b_2,
  output c_2,
  output d_2
);

  wire and_1_out, and_2_out, and_3_out, and_4_out, and_5_out, and_6_out, and_7_out, and_8_out, and_9_out,
       and_10_out, and_11_out, and_12_out, and_13_out, and_14_out, and_15_out, and_16_out, and_17_out,
       and_18_out, and_19_out, and_20_out, and_21_out, and_22_out, and_23_out, and_24_out, and_25_out,
       and_26_out, and_27_out, and_28_out, and_29_out, and_30_out, and_31_out, and_32_out, and_33_out,
       and_34_out, and_35_out, and_36_out, and_37_out, and_38_out, and_39_out, not_1_out, not_2_out,
       not_3_out, not_4_out, not_5_out, not_6_out, not_7_out, not_8_out, not_9_out, not_10_out, not_11_out,
       not_12_out, not_13_out, not_14_out, not_15_out, not_16_out, not_17_out, not_18_out, not_19_out,
       not_20_out, not_21_out, not_22_out, not_23_out, not_24_out, not_25_out, not_26_out, not_27_out,
       not_28_out, not_29_out, not_30_out, not_31_out, not_32_out, not_33_out, not_34_out, not_35_out,
       not_36_out, not_37_out, not_38_out, not_39_out, not_40_out, not_41_out, not_42_out, not_43_out,
       not_44_out, not_45_out, not_46_out, not_47_out, not_48_out, not_49_out, not_50_out, not_51_out,
       not_52_out, not_53_out, not_54_out, not_55_out, not_56_out, not_57_out, not_58_out, not_59_out,
       not_60_out, not_61_out, not_62_out, not_63_out, not_64_out, not_65_out, not_66_out, not_67_out,
       not_68_out, not_69_out, not_70_out, not_71_out, not_72_out, not_73_out, not_74_out, not_75_out,
       not_76_out, not_77_out, not_78_out, not_79_out, not_80_out, not_81_out, not_82_out, not_83_out,
       not_84_out, not_85_out, not_86_out, not_87_out, not_88_out, not_89_out, not_90_out;

  not not_1 (not_1_out, a);
  not not_2 (not_2_out, c);
  not not_3 (not_3_out, a);
  not not_4 (not_4_out, e);
  not not_5 (not_5_out, c);
  not not_6 (not_6_out, e);
  not not_7 (not_7_out, a);
  not not_8 (not_8_out, d);
  not not_9 (not_9_out, b);
  not not_10 (not_10_out, d);
  not not_11 (not_11_out, b);
  not not_12 (not_12_out, e);
  not not_13 (not_13_out, a);
  not not_14 (not_14_out, b);
  not not_15 (not_15_out, d);
  not not_16 (not_16_out, a);
  not not_17 (not_17_out, b);
  not not_18 (not_18_out, e);
  not not_19 (not_19_out, b);
  not not_20 (not_20_out, c);
  not not_21 (not_21_out, e);
  not not_22 (not_22_out, a);
  not not_23 (not_23_out, c);
  not not_24 (not_24_out, d);
  not not_25 (not_25_out, a);
  not not_26 (not_26_out, c);
  not not_27 (not_27_out, e);
  not not_28 (not_28_out, a);
  not not_29 (not_29_out, d);
  not not_30 (not_30_out, e);
  not not_31 (not_31_out, a);
  not not_32 (not_32_out, b);
  not not_33 (not_33_out, d);
  not not_34 (not_34_out, e);
  not not_35 (not_35_out, b);
  not not_36 (not_36_out, c);
  not not_37 (not_37_out, d);
  not not_38 (not_38_out, e);
  not not_39 (not_39_out, a);
  not not_40 (not_40_out, b);
  not not_41 (not_41_out, c);
  not not_42 (not_42_out, e);
  not not_43 (not_43_out, a);
  not not_44 (not_44_out, b);
  not not_45 (not_45_out, d);
  not not_46 (not_46_out, a);
  not not_47 (not_47_out, c);
  not not_48 (not_48_out, d);
  not not_49 (not_49_out, e);
  not not_50 (not_50_out, a);
  not not_51 (not_51_out, c);
  not not_52 (not_52_out, a);
  not not_53 (not_53_out, e);
  not not_54 (not_54_out, b);
  not not_55 (not_55_out, c);
  not not_56 (not_56_out, d);
  not not_57 (not_57_out, b);
  not not_58 (not_58_out, d);
  not not_59 (not_59_out, e);
  not not_60 (not_60_out, b);
  not not_61 (not_61_out, c);
  not not_62 (not_62_out, e);
  not not_63 (not_63_out, d);
  not not_64 (not_64_out, a);
  not not_65 (not_65_out, b);
  not not_66 (not_66_out, c);
  not not_67 (not_67_out, d);
  not not_68 (not_68_out, a);
  not not_69 (not_69_out, b);
  not not_70 (not_70_out, d);
  not not_71 (not_71_out, e);
  not not_72 (not_72_out, a);
  not not_73 (not_73_out, b);
  not not_74 (not_74_out, a);
  not not_75 (not_75_out, c);
  not not_76 (not_76_out, e);
  not not_77 (not_77_out, a);
  not not_78 (not_78_out, d);
  not not_79 (not_79_out, b);
  not not_80 (not_80_out, c);
  not not_81 (not_81_out, d);
  not not_82 (not_82_out, e);
  not not_83 (not_83_out, b);
  not not_84 (not_84_out, c);
  not not_85 (not_85_out, b);
  not not_86 (not_86_out, e);
  not not_87 (not_87_out, c);
  not not_88 (not_88_out, d);
  not not_89 (not_89_out, d);
  not not_90 (not_90_out, e);
  and and_1 (and_1_out, not_1_out, b, not_2_out, d);
  and and_2 (and_2_out, not_3_out, b, d, not_4_out);
  and and_3 (and_3_out, b, not_5_out, d, not_6_out);
  and and_4 (and_4_out, not_7_out, b, c, not_8_out, e);
  and and_5 (and_5_out, a, not_9_out, c, not_10_out, e);
  and and_6 (and_6_out, a, not_11_out, c, d, not_12_out);
  and and_7 (and_7_out, not_13_out, not_14_out, not_15_out, e);
  and and_8 (and_8_out, not_16_out, not_17_out, d, not_18_out);
  and and_9 (and_9_out, not_19_out, not_20_out, d, not_21_out);
  and and_10 (and_10_out, not_22_out, b, not_23_out, not_24_out);
  and and_11 (and_11_out, not_25_out, b, not_26_out, not_27_out);
  and and_12 (and_12_out, not_28_out, b, not_29_out, not_30_out);
  and and_13 (and_13_out, not_31_out, b, c, d, e);
  and and_14 (and_14_out, a, not_32_out, c, not_33_out, not_34_out);
  and and_15 (and_15_out, a, not_35_out, c, d, e);
  and and_16 (and_16_out, a, b, not_36_out, d, e);
  and and_17 (and_17_out, a, b, c, not_37_out, e);
  and and_18 (and_18_out, a, b, c, d, not_38_out);
  and and_19 (and_19_out, not_39_out, not_40_out, not_41_out, d, not_42_out);
  and and_20 (and_20_out, not_43_out, not_44_out, c, not_45_out, e);
  and and_21 (and_21_out, not_46_out, b, not_47_out, not_48_out, not_49_out);
  and and_22 (and_22_out, not_50_out, b, not_51_out, d, e);
  and and_23 (and_23_out, not_52_out, b, c, d, not_53_out);
  and and_24 (and_24_out, a, not_54_out, not_55_out, not_56_out, e);
  and and_25 (and_25_out, a, not_57_out, c, not_58_out, not_59_out);
  and and_26 (and_26_out, a, not_60_out, c, d, e);
  and and_27 (and_27_out, a, b, not_61_out, d, not_62_out);
  and and_28 (and_28_out, a, b, c, not_63_out, e);
  and and_29 (and_29_out, not_64_out, not_65_out, not_66_out, not_67_out, e);
  and and_30 (and_30_out, not_68_out, not_69_out, c, not_70_out, not_71_out);
  and and_31 (and_31_out, not_72_out, not_73_out, c, d, e);
  and and_32 (and_32_out, not_74_out, b, not_75_out, d, not_76_out);
  and and_33 (and_33_out, not_77_out, b, c, not_78_out, e);
  and and_34 (and_34_out, a, not_79_out, not_80_out, not_81_out, not_82_out);
  and and_35 (and_35_out, a, not_83_out, not_84_out, d, e);
  and and_36 (and_36_out, a, not_85_out, c, d, not_86_out);
  and and_37 (and_37_out, a, b, not_87_out, not_88_out, e);
  and and_38 (and_38_out, a, b, c, not_89_out, not_90_out);
  and and_39 (and_39_out, a, b, c, d, e);
  or or_1 (a_2, and_1_out, and_2_out, and_3_out, and_4_out, and_5_out, and_6_out);
  or or_2 (b_2, and_7_out, and_8_out, and_9_out, and_10_out, and_11_out, and_12_out, and_13_out, and_14_out, and_15_out, and_16_out, and_17_out, and_18_out);
  or or_3 (c_2, and_19_out, and_20_out, and_21_out, and_22_out, and_23_out, and_24_out, and_25_out, and_26_out, and_27_out, and_28_out);
  or or_4 (d_2, and_29_out, and_30_out, and_31_out, and_32_out, and_33_out, and_34_out, and_35_out, and_36_out, and_37_out, and_38_out, and_39_out);
endmodule
