// Logisim project lab_6.circ as structural Verilog: 7 circuits, main circuit Схема сравнения
module \Схема_сравнения  (
  input  in_1,
  input  in_2,
  output out_3
);

  wire and_1_out, and_2_out, not_1_out, not_2_out;

  not not_1 (not_1_out, in_1);
  not not_2 (not_2_out, in_2);
  and and_1 (and_1_out, not_1_out, in_2);
  and and_2 (and_2_out, in_1, not_2_out);
  or or_1 (out_3, and_1_out, and_2_out);

  // Notes on the sheet:
  //   Схема сравнения
endmodule

module \Полусумматор  (
  input  in_1,
  input  in_2,
  output out_3,
  output out_4
);

  \Схема_сравнения  \u_схема_сравнения_1  (.in_1(in_1), .in_2(in_2), .out_3(out_4));
  and and_1 (out_3, in_1, in_2);

  // Notes on the sheet:
  //   Полусумматор
endmodule

module \Полный_сумматор  (
  input  in_1,
  input  in_2,
  input  in_3,
  output out_4,
  output out_5
);

  wire \полусумматор_1_out_3 , \полусумматор_1_out_4 , \полусумматор_2_out_3 ;

  \Полусумматор  \u_полусумматор_1  (
    .in_1(in_1), .in_2(in_2), .out_3(\полусумматор_1_out_3 ), .out_4(\полусумматор_1_out_4 ));
  \Полусумматор  \u_полусумматор_2  (
    .in_1(\полусумматор_1_out_4 ), .in_2(in_3), .out_3(\полусумматор_2_out_3 ), .out_4(out_5));
  or or_1 (out_4, \полусумматор_1_out_3 , \полусумматор_2_out_3 );

  // Notes on the sheet:
  //   Cумматор
endmodule

module \Схема_4_сумматоров  (
  input  X4,
  input  Y4,
  input  X3,
  input  Y3,
  input  X2,
  input  Y2,
  input  X1,
  input  Y1,
  input  P0,
  output P4,
  output S4,
  output S3,
  output S2,
  output S1
);

  wire \полный_сумматор_1_out_4 , \полный_сумматор_2_out_4 , \полный_сумматор_3_out_4 ;

  \Полный_сумматор  \u_полный_сумматор_1  (
    .in_1(X1), .in_2(Y1), .in_3(P0), .out_4(\полный_сумматор_1_out_4 ), .out_5(S1));
  \Полный_сумматор  \u_полный_сумматор_2  (
    .in_1(X2), .in_2(Y2), .in_3(\полный_сумматор_1_out_4 ), .out_4(\полный_сумматор_2_out_4 ), .out_5(S2));
  \Полный_сумматор  \u_полный_сумматор_3  (
    .in_1(X3), .in_2(Y3), .in_3(\полный_сумматор_2_out_4 ), .out_4(\полный_сумматор_3_out_4 ), .out_5(S3));
  \Полный_сумматор  \u_полный_сумматор_4  (
    .in_1(X4), .in_2(Y4), .in_3(\полный_сумматор_3_out_4 ), .out_4(P4), .out_5(S4));

  // Notes on the sheet:
  //   Схема 4 сумматоров
  //   S5
endmodule

module \Полный_сумматор__по_таблице  (
  input  a,
  input  b,
  input  p,
  output P_2,
  output S
);

  wire and_1_out, and_2_out, and_3_out, and_4_out, and_5_out, and_6_out, and_7_out, not_1_out, not_2_out,
       not_3_out, not_4_out, not_5_out, not_6_out;

  and and_1 (and_1_out, b, p);
  and and_2 (and_2_out, a, p);
  and and_3 (and_3_out, a, b);
  not not_1 (not_1_out, a);
  not not_2 (not_2_out, b);
  not not_3 (not_3_out, a);
  not not_4 (not_4_out, p);
  not not_5 (not_5_out, b);
  not not_6 (not_6_out, p);
  or or_1 (P_2, and_1_out, and_2_out, and_3_out);
  and and_4 (and_4_out, not_1_out, not_2_out, p);
  and and_5 (and_5_out, not_3_out, b, not_4_out);
  and and_6 (and_6_out, a, not_5_out, not_6_out);
  and and_7 (and_7_out, a, b, p);
  or or_2 (S, and_4_out, and_5_out, and_6_out, and_7_out);
endmodule

module \Полусумматор__по_таблице  (
  input  a,
  input  b,
  output P,
  output S
);

  wire and_2_out, and_3_out, not_1_out, not_2_out;

  and and_1 (P, a, b);
  not not_1 (not_1_out, a);
  not not_2 (not_2_out, b);
  and and_2 (and_2_out, not_1_out, b);
  and and_3 (and_3_out, a, not_2_out);
  or or_1 (S, and_2_out, and_3_out);
endmodule

module \Схема_8_сумматоров  (
  input  X8,
  input  Y8,
  input  X7,
  input  Y7,
  input  X6,
  input  Y6,
  input  X5,
  input  Y5,
  input  X4,
  input  Y4,
  input  X3,
  input  Y3,
  input  X2,
  input  Y2,
  input  X1,
  input  Y1,
  input  P0,
  output out_18,
  output S4,
  output S3,
  output S2,
  output S1,
  output out_23,
  output S4_2,
  output S3_2,
  output S2_2,
  output S1_2
);

  wire \полный_сумматор_1_out_4 , \полный_сумматор_2_out_4 , \полный_сумматор_3_out_4 ,
       \полный_сумматор_5_out_4 , \полный_сумматор_6_out_4 , \полный_сумматор_7_out_4 ;

  \Полный_сумматор  \u_полный_сумматор_1  (
    .in_1(X1), .in_2(Y1), .in_3(P0), .out_4(\полный_сумматор_1_out_4 ), .out_5(S1_2));
  \Полный_сумматор  \u_полный_сумматор_2  (
    .in_1(X3), .in_2(Y3), .in_3(\полный_сумматор_3_out_4 ), .out_4(\полный_сумматор_2_out_4 ), .out_5(S3_2));
  \Полный_сумматор  \u_полный_сумматор_3  (
    .in_1(X2), .in_2(Y2), .in_3(\полный_сумматор_1_out_4 ), .out_4(\полный_сумматор_3_out_4 ), .out_5(S2_2));
  \Полный_сумматор  \u_полный_сумматор_4  (
    .in_1(X4), .in_2(Y4), .in_3(\полный_сумматор_2_out_4 ), .out_4(out_23), .out_5(S4_2));
  \Полный_сумматор  \u_полный_сумматор_5  (
    .in_1(X5), .in_2(Y5), .out_4(\полный_сумматор_5_out_4 ), .out_5(S1));  // open: in_3
  \Полный_сумматор  \u_полный_сумматор_6  (
    .in_1(X6), .in_2(Y6), .in_3(\полный_сумматор_5_out_4 ), .out_4(\полный_сумматор_6_out_4 ), .out_5(S2));
  \Полный_сумматор  \u_полный_сумматор_7  (
    .in_1(X7), .in_2(Y7), .in_3(\полный_сумматор_6_out_4 ), .out_4(\полный_сумматор_7_out_4 ), .out_5(S3));
  \Полный_сумматор  \u_полный_сумматор_8  (
    .in_1(X8), .in_2(Y8), .in_3(\полный_сумматор_7_out_4 ), .out_4(out_18), .out_5(S4));

  // Notes on the sheet:
  //   Схема 8 сумматоров
endmodule
