// Logisim project lab_7.circ as structural Verilog: 5 circuits, main circuit 2х канальный мультиплексор
module \_2х_канальный_мультиплексор  (
  input  in_1,
  input  in_2,
  input  in_3,
  output out_4
);

  wire and_1_out, and_2_out, not_1_out;

  not not_1 (not_1_out, in_3);
  and and_1 (and_1_out, in_1, not_1_out);
  and and_2 (and_2_out, in_2, in_3);
  or or_1 (out_4, and_1_out, and_2_out);

  // Notes on the sheet:
  //   2х канальный мультиплексор
endmodule

module \_4х_канальный_мультиплексор  (
  input  in_1,
  input  in_2,
  input  in_3,
  input  in_4,
  input  in_5,
  input  in_6,
  output out_7
);

  wire and_1_out, and_2_out, and_3_out, and_4_out, not_1_out, not_2_out;

  not not_1 (not_1_out, in_1);
  not not_2 (not_2_out, in_2);
  and and_1 (and_1_out, not_1_out, not_2_out, in_3);
  and and_2 (and_2_out, not_2_out, in_1, in_4);
  and and_3 (and_3_out, not_1_out, in_5, in_2);
  and and_4 (and_4_out, in_1, in_6, in_2);
  or or_1 (out_7, and_1_out, and_2_out, and_3_out, and_4_out);

  // Notes on the sheet:
  //   4х канальный мультиплексор
endmodule

module \_16ти_канальный_мультиплексор  (
  input  in_1,
  input  in_2,
  input  in_3,
  input  in_4,
  input  in_5,
  input  in_6,
  input  in_7,
  input  in_8,
  input  in_9,
  input  in_10,
  input  in_11,
  input  in_12,
  input  in_13,
  input  in_14,
  input  in_15,
  input  in_16,
  input  in_17,
  input  in_18,
  input  in_19,
  input  in_20,
  output out_21
);

  wire \n4х_канальный_мультиплексор_1_out_7 , \n4х_канальный_мультиплексор_2_out_7 ,
       \n4х_канальный_мультиплексор_3_out_7 , \n4х_канальный_мультиплексор_4_out_7 ;

  \_4х_канальный_мультиплексор  \u_4х_канальный_мультиплексор_1  (
    .in_1(in_17), .in_2(in_18), .in_3(in_1), .in_4(in_2), .in_5(in_3), .in_6(in_4),
    .out_7(\n4х_канальный_мультиплексор_1_out_7 ));
  \_4х_канальный_мультиплексор  \u_4х_канальный_мультиплексор_2  (
    .in_1(in_17), .in_2(in_18), .in_3(in_5), .in_4(in_6), .in_5(in_7), .in_6(in_8),
    .out_7(\n4х_канальный_мультиплексор_2_out_7 ));
  \_4х_канальный_мультиплексор  \u_4х_канальный_мультиплексор_3  (
    .in_1(in_17), .in_2(in_18), .in_3(in_9), .in_4(in_10), .in_5(in_11), .in_6(in_12),
    .out_7(\n4х_канальный_мультиплексор_3_out_7 ));
  \_4х_канальный_мультиплексор  \u_4х_канальный_мультиплексор_4  (
    .in_1(in_17), .in_2(in_18), .in_3(in_13), .in_4(in_14), .in_5(in_15), .in_6(in_16),
    .out_7(\n4х_канальный_мультиплексор_4_out_7 ));
  \_4х_канальный_мультиплексор  \u_4х_канальный_мультиплексор_5  (
    .in_1(in_19), .in_2(in_20), .in_3(\n4х_канальный_мультиплексор_1_out_7 ),
    .in_4(\n4х_канальный_мультиплексор_2_out_7 ), .in_5(\n4х_канальный_мультиплексор_3_out_7 ),
    .in_6(\n4х_канальный_мультиплексор_4_out_7 ), .out_7(out_21));

  // Notes on the sheet:
  //   16ти канальный мультиплексор
endmodule

module \Демультиплексор  (
  input  in_1,
  input  in_2,
  output out_3,
  output out_4
);

  wire not_1_out;

  not not_1 (not_1_out, in_2);
  and and_1 (out_3, in_1, not_1_out);
  and and_2 (out_4, in_1, in_2);

  // Notes on the sheet:
  //   Демультиплексор
endmodule

module \_16ти_канальный_мультиплексор__из_стандартных_элементов  (
  input  in_1,
  input  in_2,
  input  in_3,
  input  in_4,
  input  in_5,
  input  in_6,
  input  in_7,
  input  in_8,
  input  in_9,
  input  in_10,
  input  in_11,
  input  in_12,
  input  in_13,
  input  in_14,
  input  in_15,
  input  in_16,
  input  [1:0] in_17,
  input  [1:0] in_18,
  output out_19
);

  wire multiplexer_1_out, multiplexer_2_out, multiplexer_3_out, multiplexer_4_out;

  Multiplexer #(.select(2), .enable("false")) multiplexer_1 (
    .in0(in_1), .in1(in_2), .in2(in_3), .in3(in_4), .out(multiplexer_1_out), .sel(in_17));
  Multiplexer #(.select(2), .enable("false")) multiplexer_2 (
    .in0(in_5), .in1(in_6), .in2(in_7), .in3(in_8), .out(multiplexer_2_out), .sel(in_17));
  Multiplexer #(.select(2), .enable("false")) multiplexer_3 (
    .in0(in_9), .in1(in_10), .in2(in_11), .in3(in_12), .out(multiplexer_3_out), .sel(in_17));
  Multiplexer #(.select(2), .enable("false")) multiplexer_4 (
    .in0(in_13), .in1(in_14), .in2(in_15), .in3(in_16), .out(multiplexer_4_out), .sel(in_17));
  Multiplexer #(.select(2), .enable("false")) multiplexer_5 (
    .in0(multiplexer_1_out), .in1(multiplexer_2_out), .in2(multiplexer_3_out), .in3(multiplexer_4_out),
    .out(out_19), .sel(in_18));

  // Notes on the sheet:
  //   16ти канальный мультиплексор
endmodule
