// Logisim project lab_8.circ as structural Verilog: 1 circuit, main circuit main
module main (
  input  [7:0] in_1,
  input  in_2
);

  wire button_1_out, demultiplexer_1_out0, demultiplexer_1_out1, demultiplexer_1_out2, demultiplexer_1_out3;
  wire [1:0] counter_1_q;
  wire [7:0] register_1_q;

  Demultiplexer #(.select(2)) demultiplexer_1 (
    .out0(demultiplexer_1_out0), .out1(demultiplexer_1_out1), .out2(demultiplexer_1_out2),
    .out3(demultiplexer_1_out3), .in(in_2), .sel(counter_1_q));  // open: en
  Counter #(.width(2), .max('h0)) counter_1 (.Q(counter_1_q), .clk(button_1_out));  // open: load, D, count, carry, clr
  Button button_1 (.out(button_1_out));
  Register register_1 (.D(in_1), .Q(register_1_q), .clk(demultiplexer_1_out0));  // open: en, clr
  Register register_2 (.D(in_1), .clk(demultiplexer_1_out1));  // open: en, Q, clr
  Register register_3 (.D(in_1), .clk(demultiplexer_1_out2));  // open: en, Q, clr
  Register register_4 (.D(in_1), .clk(demultiplexer_1_out3));  // open: en, Q, clr
  Multiplexer multiplexer_1 ();  // open: in0, in1, out, sel, en
endmodule
